# Fritzing sketch basic module_v2 (saved by Fritzing 1.0.6)
circuit board: 6.95673cm x 7.41371cm
breadboards: 2

parts:
  A1 = ESP32-S3-1-N16R8-module
  POWER = Camdenboss CTB0158-2 [part_number=CTB0158-2 package=THT]
  J4 = Dagu DGServo 9g header (male) [package=THT]
  J5 = Dagu DGServo 9g header (male) [package=THT]
  U1 = JST XH 3A Male [chip_label=? package=THT]
  I2c = JST XH 3A Male [chip_label=? package=THT]
  LCD1 = 1.28 inch Round 240x240 LCD Display
  LCD2 = 1.28 inch Round 240x240 LCD Display
  J6 = Dagu DGServo 9g header (male) [package=THT]
  J7 = Dagu DGServo 9g header (male) [package=THT]

nets:
  N1: A1.Pin_1, LCD1.Pin_6, LCD1.Pin_13, LCD2.Pin_6, LCD2.Pin_13, J7.gnd
  N2: A1.Pin_6, J4.gnd
  N3: A1.Pin_8, J5.gnd
  N4: A1.Pin_9, U1.pin2
  N5: A1.Pin_10, U1.pin1
  N6: A1.Pin_11, I2c.pin2
  N7: A1.Pin_14, I2c.pin1
  N8: A1.Pin_20, POWER.pin2, J4.pulse, J5.pulse, J6.gnd
  VCC: A1.Pin_21, POWER.pin1, J4.Vcc, J5.Vcc, U1.pin3, I2c.pin3, LCD1.Pin_7, LCD2.Pin_7, J6.Vcc, J7.Vcc
  N9: A1.Pin_24, J7.pulse
  N10: A1.Pin_25, J6.pulse
  N11: A1.Pin_32, LCD1.Pin_12, LCD2.Pin_12
  N12: A1.Pin_33, LCD1.Pin_11, LCD2.Pin_11
  N13: A1.Pin_34, LCD1.Pin_10, LCD2.Pin_10
  N14: A1.Pin_35, LCD1.Pin_9, LCD2.Pin_9
  N15: A1.Pin_37, LCD1.Pin_8
  N16: A1.Pin_38, LCD2.Pin_8

notes:
  +
  -
  5V
  GND
  ADC(G7)
  DIO(16)
  RPI
  UART
  POWER
  RX
  TX
  SDA
  SCL
  OL
  OLAF
  ESP32
  N16R8
  AF
  3.3V
  IO21
  IO47
  OPTCPLR
  LNRSVO
  R.EYE
  L.EYE
  Kamal Singh
  BL
  Ear Servo
  EYES
  Proj. Cont.
  Servo CNT.
  HEAD Module

custom parts:
  ESP32-S3-1-N16R8-module: ESP32-S3 CAM development board WiFi Bluetooth module onboard ESP32-S3-1 N16R8 module dual TYPE-C interface.
  JST XH 3A Male: 2.54 Mm JST "XH" connector
  1.28 inch Round 240x240 LCD Display: TFT Display 1.28 Inch TFT LCD Display Module Round RGB 240*240 GC9A01 Driver 4 Wire SPI Interface 240x240.
