# Fritzing sketch neck module (saved by Fritzing 1.0.6)
circuit board: 7.34479cm x 6.99461cm
breadboards: 2

parts:
  A1 = ESP32-S3-1-N16R8-module
  POWER = Camdenboss CTB0158-2 [part_number=CTB0158-2 package=THT]
  J4 = Dagu DGServo 9g header (male) [package=THT]
  J5 = Dagu DGServo 9g header (male) [package=THT]
  U1 = JST XH 3A Male [chip_label=? package=THT]
  I2c = JST XH 3A Male [chip_label=? package=THT]
  J7 = Dagu DGServo 9g header (male) [package=THT]
  J8 = Dagu DGServo 9g header (male) [package=THT]
  J9 = Dagu DGServo 9g header (male) [package=THT]
  U2 = mystery part, 4 pins [chip_label=?]
  J10 = Dagu DGServo 9g header (male) [package=THT]
  C1 = Capacitor Polarized [package=cpol-radial-100uf-25v]

nets:
  N1: A1.Pin_6, J4.gnd
  N2: A1.Pin_8, J5.gnd
  N3: A1.Pin_9, U1.pin2
  N4: A1.Pin_10, U1.pin1
  N5: A1.Pin_11, I2c.pin2
  N6: A1.Pin_14, I2c.pin1
  GND: A1.Pin_20, POWER.pin2, J4.pulse, J5.pulse, J7.gnd, J8.gnd, J9.gnd, U2.pin4, J10.gnd, C1.+
  VCC: A1.Pin_21, POWER.pin1, J4.Vcc, J5.Vcc, U1.pin3, I2c.pin3, J7.Vcc, J8.Vcc, J9.Vcc, U2.pin3, J10.Vcc, C1.-
  N7: A1.Pin_27, J7.pulse
  N8: A1.Pin_28, J8.pulse
  N9: A1.Pin_29, J9.pulse
  N10: A1.Pin_32, U2.pin1
  N11: A1.Pin_33, U2.pin2
  N12: A1.Pin_38, J10.pulse

notes:
  +
  -
  5V
  GND
  ADC(G7)
  DIO(16)
  RPI
  UART
  POWER
  RX
  TX
  SDA
  SCL
  OL
  Kamal Singh
  OLAF
  ESP32
  N16R8
  AF
  Servo Cont.
  MM Sensor
  45
  0
  35
  Neck Module
  WS2812 strip
  DIN
  Front
  neck servos
  Kickstand
  Status LEDs

custom parts:
  ESP32-S3-1-N16R8-module: ESP32-S3 CAM development board WiFi Bluetooth module onboard ESP32-S3-1 N16R8 module dual TYPE-C interface.
  JST XH 3A Male: 2.54 Mm JST "XH" connector
