# Fritzing sketch I2C_pullup (saved by Fritzing 1.0.6)
circuit board: 4.89865cm x 1.98162cm
breadboards: 1

parts:
  R1 = Resistor [tolerance=±5% power=0.25W resistance=220 package=THT]
  R2 = Resistor [tolerance=±5% power=0.25W resistance=220 package=THT]
  U1 = mystery part, 4 pins [chip_label=?]
  U2 = JST XH 3A Male [chip_label=? package=THT]
  U3 = JST XH 3A Male [chip_label=? package=THT]
  U4 = JST XH 3A Male [chip_label=? package=THT]
  U5 = JST XH 3A Male [chip_label=? package=THT]
  U6 = JST XH 3A Male [chip_label=? package=THT]
  U7 = JST XH 3A Male [chip_label=? package=THT]
  U8 = JST XH 3A Male [chip_label=? package=THT]
  U9 = JST XH 3A Male [chip_label=? package=THT]
  U10 = JST XH 3A Male [chip_label=? package=THT]
  U11 = JST XH 3A Male [chip_label=? package=THT]

nets:
  N1: R1.Pin_0, R2.Pin_0, U1.pin1
  N2: R1.Pin_1, U1.pin3, U2.pin2, U3.pin2, U4.pin2, U5.pin2, U6.pin2, U7.pin2, U8.pin2, U9.pin2, U10.pin2, U11.pin2
  N3: R2.Pin_1, U1.pin2, U2.pin1, U3.pin1, U4.pin1, U5.pin1, U6.pin1, U7.pin1, U8.pin1, U9.pin1, U10.pin1, U11.pin1
  N4: U1.pin4, U2.pin3, U3.pin3, U4.pin3, U5.pin3, U6.pin3, U7.pin3, U8.pin3, U9.pin3, U10.pin3, U11.pin3

notes:
  3.3V
  GND
  SCL
  SDA
  R - 4.7K
  OLAF

custom parts:
  JST XH 3A Male: 2.54 Mm JST "XH" connector
