# Fritzing sketch torso module (saved by Fritzing 1.0.6)
circuit board: 7.49271cm x 7.94961cm
breadboards: 2

parts:
  A1 = ESP32-S3-1-N16R8-module
  POWER = Camdenboss CTB0158-2 [part_number=CTB0158-2 package=THT]
  J4 = Dagu DGServo 9g header (male) [package=THT]
  J5 = Dagu DGServo 9g header (male) [package=THT]
  U1 = JST XH 3A Male [chip_label=? package=THT]
  I2c = JST XH 3A Male [chip_label=? package=THT]
  J7 = Dagu DGServo 9g header (male) [package=THT]
  J8 = Dagu DGServo 9g header (male) [package=THT]
  J9 = Dagu DGServo 9g header (male) [package=THT]
  U2 = mystery part, 4 pins [chip_label=?]
  LCD1 = 2.8" SPI TFT Module [part_number=MSP2807]  # not connected
  J10 = Dagu DGServo 9g header (male) [package=THT]  # not connected
  U3 = mystery part, 8 pins [chip_label=?]

nets:
  N1: A1.Pin_6, J4.gnd
  N2: A1.Pin_8, J5.gnd
  N3: A1.Pin_9, U1.pin2
  N4: A1.Pin_10, U1.pin1
  N5: A1.Pin_11, I2c.pin2
  N6: A1.Pin_14, I2c.pin1
  N7: A1.Pin_18, U3.pin6
  N8: A1.Pin_19, U3.pin7
  GND: A1.Pin_20, POWER.pin2, J4.pulse, J5.pulse, J7.gnd, J8.gnd, J9.gnd, U2.pin4, U3.pin1
  VCC: A1.Pin_21, POWER.pin1, J4.Vcc, J5.Vcc, U1.pin3, I2c.pin3, J7.Vcc, J8.Vcc, J9.Vcc, U2.pin3, U3.pin2
  N9: A1.Pin_24, U3.pin5
  N10: A1.Pin_25, U3.pin3
  N11: A1.Pin_27, J7.pulse
  N12: A1.Pin_28, J8.pulse
  N13: A1.Pin_29, J9.pulse
  N14: A1.Pin_32, U2.pin1
  N15: A1.Pin_33, U2.pin2
  N16: A1.Pin_36, U3.pin8
  N17: A1.Pin_37, U3.pin4

notes:
  +
  -
  5V
  GND
  ADC(G7)
  DIO(16)
  RPI
  UART
  POWER
  RX
  TX
  SDA
  SCL
  OL
  Kamal Singh
  OLAF
  ESP32
  N16R8
  AF
  TH PRNTR
  MM pres. (back)
  45
  0
  35
  Heart LCD
  MM pres (back)
  Th. Printer
  Torso
  CS
  RST
  DC
  MOSI
  SCK
  LED
  Body LCD

custom parts:
  ESP32-S3-1-N16R8-module: ESP32-S3 CAM development board WiFi Bluetooth module onboard ESP32-S3-1 N16R8 module dual TYPE-C interface.
  JST XH 3A Male: 2.54 Mm JST "XH" connector
  2.8" SPI TFT Module: A generic 2.8 inch LCD TFT 320x240 display with touchscreen and SD card slot. Uses the ILI9341 controller, like the Adafruit displays of this size uses.
